# Fritzing sketch diagram_JonathanElizabeth (saved by Fritzing 0.9.3b)
breadboards: 1

parts:
  Part1 = Arduino Uno (Rev3)
  J1 = Basic Servo
  J2 = Basic Servo

nets:
  N1: Part1.D9_PWM, J1.pulse
  N2: Part1.D10_PWM/SS, J2.pulse
  VCC: Part1.5V, J1.vcc, J2.vcc
  GND: Part1.GND, J1.gnd, J2.gnd
